# Fritzing sketch display (saved by Fritzing 0.8.7b)
breadboards: 1

parts:
  U1 = 7-SEGMENT-4DIGIT [package=7-segment-4digit]
  R1 = Resistor [tolerance=±5% resistance=220 package=THT]
  R2 = Resistor [tolerance=±5% resistance=330 package=THT]
  R3 = Resistor [tolerance=±5% resistance=330 package=THT]
  R4 = Resistor [tolerance=±5% resistance=330 package=THT]
  R5 = Resistor [tolerance=±5% resistance=330 package=THT]
  R6 = Resistor [tolerance=±5% resistance=330 package=THT]
  R7 = Resistor [tolerance=±5% resistance=330 package=THT]
  R8 = Resistor [tolerance=±5% resistance=330 package=THT]
  R9 = Resistor [tolerance=±5% resistance=330 package=THT]

nets:
  N1: U1.3, R1.Pin_1
  N2: U1.4, R3.Pin_0
  N3: U1.5, R2.Pin_0
  N4: U1.7, R4.Pin_1
  N5: U1.8, R2.Pin_1
  N6: U1.11, R5.Pin_0
  N7: U1.13, R6.Pin_1
  N8: U1.14, R7.Pin_1
  N9: U1.15, R8.Pin_1
  N10: U1.16, R9.Pin_1
